# Fritzing sketch nozzles schematic (saved by Fritzing 0.9.9b)

parts:
  J1 = STM32 Nucleo boards
  J2 = Dagu DGServo 9g header (male) [package=THT]
  A1 = 2957N11 pressure sensor
  R1 = Rotary Potentiometer (Large) [maximum_resistance=100kΩ package=THT]
  R2 = Rotary Potentiometer (Large) [maximum_resistance=100kΩ package=THT]
  R3 = Rotary Potentiometer (Large) [maximum_resistance=100kΩ package=THT]
  R4 = Rotary Potentiometer (Large) [maximum_resistance=100kΩ package=THT]
  R5 = Rotary Potentiometer (Large) [maximum_resistance=100kΩ package=THT]
  R6 = Rotary Potentiometer (Large) [maximum_resistance=100kΩ package=THT]  # not connected
  U1 = ESP32S-HiLetgo [part_number=ESP32S-HiLetgo]
  Mod1 = KY-022 Infrared Receiver Module [package="Breakout board"]
  Part1 = LCD1602-I2C

nets:
  N1: J1.PA11, Mod1.S
  VIN: J1.3v3, J2.Vcc, U1.VIN, Mod1.Vin
  5V: J1.5V, J2.pulse, A1.Pin_2, R1.leg1, R2.leg1, R3.leg1, R4.leg1, R5.leg1, Part1.VCC
  GND: J1.GND, J2.gnd, A1.Pin_1, R1.leg2, R2.leg2, R3.leg2, R4.leg2, R5.leg2, U1.GND, Mod1.-, Part1.GND
  N2: J1.D10_PWM/SS, U1.GPIO16
  N3: J1.D1/TX, U1.GPIO17
  N4: J1.D3_PWM, Part1.SDA
  N5: J1.D6_PWM, Part1.SCL
  N6: J1.PA6, R4.wiper
  N7: J1.PA7, R5.wiper
  N8: J1.PA0, A1.Pin_3
  N9: J1.PA1, R1.wiper
  N10: J1.PC1, R2.wiper
  N11: J1.PC0, R3.wiper

custom parts:
  2957N11 pressure sensor: Monitor and control vacuum pumps, air compressors, and hydraulics. These transmitters convert both pressure and vacuum into an electrical signal that can be interpreted by receiving devices, such as remote displays, programmable logic controllers, and motor speed controls.
  ESP32S-HiLetgo: HiLetgo ESP-WROOM-32 ESP32 ESP-32S Development Board 2.4GHz Dual-Mode WiFi + Bluetooth Dual Cores Microcontroller The ESP32 integrated with Antenna switches, RF Balun, power amplifiers, low-noise amplifiers, filters, and management modules, and the entire solution occupies the least area of PCB. 2.4 GHz Wi-Fi plus Bluetooth dual-mode chip, with TSMC Ultra-low power consumption 40nm technology,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
  KY-022 Infrared Receiver Module: KY-022 IR receiver module, reacts to 38kHz infrared light.
  LCD1602-I2C: A standard character display, usually with 2x16 characters. Comes in many colors with LCM1602 IIC attached.
